// Logisim project processor.circ as structural Verilog: 8 circuits, main circuit Register_file
module Register_file (
  input  [4:0] rt_select,
  input  [4:0] rs_select,
  input  [31:0] rd_data,
  input  we,
  input  [4:0] rd_select,
  output [31:0] rt_data,
  output [31:0] rs_data
);

  wire clock_1_out, demultiplexer_1_out1, demultiplexer_1_out2, demultiplexer_1_out3, demultiplexer_1_out4,
       demultiplexer_1_out5, demultiplexer_1_out6, demultiplexer_1_out7, demultiplexer_1_out8,
       demultiplexer_1_out9, demultiplexer_1_out10, demultiplexer_1_out11, demultiplexer_1_out12,
       demultiplexer_1_out13, demultiplexer_1_out14, demultiplexer_1_out15, demultiplexer_1_out16,
       demultiplexer_1_out17, demultiplexer_1_out18, demultiplexer_1_out19, demultiplexer_1_out20,
       demultiplexer_1_out21, demultiplexer_1_out22, demultiplexer_1_out23, demultiplexer_1_out24,
       demultiplexer_1_out25, demultiplexer_1_out26, demultiplexer_1_out27, demultiplexer_1_out28,
       demultiplexer_1_out29, demultiplexer_1_out30, demultiplexer_1_out31;
  wire [31:0] demultiplexer_2_out1, demultiplexer_2_out2, demultiplexer_2_out3, demultiplexer_2_out4,
       demultiplexer_2_out5, demultiplexer_2_out6, demultiplexer_2_out7, demultiplexer_2_out8,
       demultiplexer_2_out9, demultiplexer_2_out10, demultiplexer_2_out11, demultiplexer_2_out12,
       demultiplexer_2_out13, demultiplexer_2_out14, demultiplexer_2_out15, demultiplexer_2_out16,
       demultiplexer_2_out17, demultiplexer_2_out18, demultiplexer_2_out19, demultiplexer_2_out20,
       demultiplexer_2_out21, demultiplexer_2_out22, demultiplexer_2_out23, demultiplexer_2_out24,
       demultiplexer_2_out25, demultiplexer_2_out26, demultiplexer_2_out27, demultiplexer_2_out28,
       demultiplexer_2_out29, demultiplexer_2_out30, demultiplexer_2_out31, reg1_q, reg2_q, reg3_q, reg4_q,
       reg5_q, reg6_q, reg7_q, reg8_q, reg9_q, reg10_q, reg11_q, reg12_q, reg13_q, reg14_q, reg15_q, reg16_q,
       reg17_q, reg18_q, reg19_q, reg20_q, reg21_q, reg22_q, reg23_q, reg24_q, reg25_q, reg26_q, reg27_q,
       reg28_q, reg29_q, reg30_q, reg31_q;

  Demultiplexer #(.enable("false"), .select(5)) demultiplexer_1 (
    .out1(demultiplexer_1_out1), .out2(demultiplexer_1_out2), .out3(demultiplexer_1_out3),
    .out4(demultiplexer_1_out4), .out5(demultiplexer_1_out5), .out6(demultiplexer_1_out6),
    .out7(demultiplexer_1_out7), .out8(demultiplexer_1_out8), .out9(demultiplexer_1_out9),
    .out10(demultiplexer_1_out10), .out11(demultiplexer_1_out11), .out12(demultiplexer_1_out12),
    .out13(demultiplexer_1_out13), .out14(demultiplexer_1_out14), .out15(demultiplexer_1_out15),
    .out16(demultiplexer_1_out16), .out17(demultiplexer_1_out17), .out18(demultiplexer_1_out18),
    .out19(demultiplexer_1_out19), .out20(demultiplexer_1_out20), .out21(demultiplexer_1_out21),
    .out22(demultiplexer_1_out22), .out23(demultiplexer_1_out23), .out24(demultiplexer_1_out24),
    .out25(demultiplexer_1_out25), .out26(demultiplexer_1_out26), .out27(demultiplexer_1_out27),
    .out28(demultiplexer_1_out28), .out29(demultiplexer_1_out29), .out30(demultiplexer_1_out30),
    .out31(demultiplexer_1_out31), .in(we), .sel(rd_select));  // open: out0
  Demultiplexer #(.select(5), .width(32)) demultiplexer_2 (
    .out1(demultiplexer_2_out1), .out2(demultiplexer_2_out2), .out3(demultiplexer_2_out3),
    .out4(demultiplexer_2_out4), .out5(demultiplexer_2_out5), .out6(demultiplexer_2_out6),
    .out7(demultiplexer_2_out7), .out8(demultiplexer_2_out8), .out9(demultiplexer_2_out9),
    .out10(demultiplexer_2_out10), .out11(demultiplexer_2_out11), .out12(demultiplexer_2_out12),
    .out13(demultiplexer_2_out13), .out14(demultiplexer_2_out14), .out15(demultiplexer_2_out15),
    .out16(demultiplexer_2_out16), .out17(demultiplexer_2_out17), .out18(demultiplexer_2_out18),
    .out19(demultiplexer_2_out19), .out20(demultiplexer_2_out20), .out21(demultiplexer_2_out21),
    .out22(demultiplexer_2_out22), .out23(demultiplexer_2_out23), .out24(demultiplexer_2_out24),
    .out25(demultiplexer_2_out25), .out26(demultiplexer_2_out26), .out27(demultiplexer_2_out27),
    .out28(demultiplexer_2_out28), .out29(demultiplexer_2_out29), .out30(demultiplexer_2_out30),
    .out31(demultiplexer_2_out31), .in(rd_data), .sel(rd_select), .en(we));  // open: out0
  Clock clock_1 (.out(clock_1_out));
  Register #(.width(32)) reg1 (
    .D(demultiplexer_2_out1), .en(demultiplexer_1_out1), .clk(clock_1_out), .Q(reg1_q));  // open: clr
  Register #(.width(32)) reg2 (
    .D(demultiplexer_2_out2), .en(demultiplexer_1_out2), .clk(clock_1_out), .Q(reg2_q));  // open: clr
  Register #(.width(32)) reg3 (
    .D(demultiplexer_2_out3), .en(demultiplexer_1_out3), .clk(clock_1_out), .Q(reg3_q));  // open: clr
  Register #(.width(32)) reg4 (
    .D(demultiplexer_2_out4), .en(demultiplexer_1_out4), .clk(clock_1_out), .Q(reg4_q));  // open: clr
  Register #(.width(32)) reg5 (
    .D(demultiplexer_2_out5), .en(demultiplexer_1_out5), .clk(clock_1_out), .Q(reg5_q));  // open: clr
  Register #(.width(32)) reg6 (
    .D(demultiplexer_2_out6), .en(demultiplexer_1_out6), .clk(clock_1_out), .Q(reg6_q));  // open: clr
  Register #(.width(32)) reg7 (
    .D(demultiplexer_2_out7), .en(demultiplexer_1_out7), .clk(clock_1_out), .Q(reg7_q));  // open: clr
  Register #(.width(32)) reg8 (
    .D(demultiplexer_2_out8), .en(demultiplexer_1_out8), .clk(clock_1_out), .Q(reg8_q));  // open: clr
  Register #(.width(32)) reg9 (
    .D(demultiplexer_2_out9), .en(demultiplexer_1_out9), .clk(clock_1_out), .Q(reg9_q));  // open: clr
  Register #(.width(32)) reg10 (
    .D(demultiplexer_2_out10), .en(demultiplexer_1_out10), .clk(clock_1_out), .Q(reg10_q));  // open: clr
  Register #(.width(32)) reg11 (
    .D(demultiplexer_2_out11), .en(demultiplexer_1_out11), .clk(clock_1_out), .Q(reg11_q));  // open: clr
  Register #(.width(32)) reg12 (
    .D(demultiplexer_2_out12), .en(demultiplexer_1_out12), .clk(clock_1_out), .Q(reg12_q));  // open: clr
  Register #(.width(32)) reg13 (
    .D(demultiplexer_2_out13), .en(demultiplexer_1_out13), .clk(clock_1_out), .Q(reg13_q));  // open: clr
  Register #(.width(32)) reg14 (
    .D(demultiplexer_2_out14), .en(demultiplexer_1_out14), .clk(clock_1_out), .Q(reg14_q));  // open: clr
  Register #(.width(32)) reg15 (
    .D(demultiplexer_2_out15), .en(demultiplexer_1_out15), .clk(clock_1_out), .Q(reg15_q));  // open: clr
  Register #(.width(32)) reg16 (
    .D(demultiplexer_2_out16), .en(demultiplexer_1_out16), .clk(clock_1_out), .Q(reg16_q));  // open: clr
  Register #(.width(32)) reg17 (
    .D(demultiplexer_2_out17), .en(demultiplexer_1_out17), .clk(clock_1_out), .Q(reg17_q));  // open: clr
  Register #(.width(32)) reg18 (
    .D(demultiplexer_2_out18), .en(demultiplexer_1_out18), .clk(clock_1_out), .Q(reg18_q));  // open: clr
  Register #(.width(32)) reg19 (
    .D(demultiplexer_2_out19), .en(demultiplexer_1_out19), .clk(clock_1_out), .Q(reg19_q));  // open: clr
  Register #(.width(32)) reg20 (
    .D(demultiplexer_2_out20), .en(demultiplexer_1_out20), .clk(clock_1_out), .Q(reg20_q));  // open: clr
  Register #(.width(32)) reg21 (
    .D(demultiplexer_2_out21), .en(demultiplexer_1_out21), .clk(clock_1_out), .Q(reg21_q));  // open: clr
  Register #(.width(32)) reg22 (
    .D(demultiplexer_2_out22), .en(demultiplexer_1_out22), .clk(clock_1_out), .Q(reg22_q));  // open: clr
  Register #(.width(32)) reg23 (
    .D(demultiplexer_2_out23), .en(demultiplexer_1_out23), .clk(clock_1_out), .Q(reg23_q));  // open: clr
  Register #(.width(32)) reg24 (
    .D(demultiplexer_2_out24), .en(demultiplexer_1_out24), .clk(clock_1_out), .Q(reg24_q));  // open: clr
  Register #(.width(32)) reg25 (
    .D(demultiplexer_2_out25), .en(demultiplexer_1_out25), .clk(clock_1_out), .Q(reg25_q));  // open: clr
  Register #(.width(32)) reg26 (
    .D(demultiplexer_2_out26), .en(demultiplexer_1_out26), .clk(clock_1_out), .Q(reg26_q));  // open: clr
  Register #(.width(32)) reg27 (
    .D(demultiplexer_2_out27), .en(demultiplexer_1_out27), .clk(clock_1_out), .Q(reg27_q));  // open: clr
  Register #(.width(32)) reg28 (
    .D(demultiplexer_2_out28), .en(demultiplexer_1_out28), .clk(clock_1_out), .Q(reg28_q));  // open: clr
  Register #(.width(32)) reg29 (
    .D(demultiplexer_2_out29), .en(demultiplexer_1_out29), .clk(clock_1_out), .Q(reg29_q));  // open: clr
  Register #(.width(32)) reg30 (
    .D(demultiplexer_2_out30), .en(demultiplexer_1_out30), .clk(clock_1_out), .Q(reg30_q));  // open: clr
  Register #(.width(32)) reg31 (
    .D(demultiplexer_2_out31), .en(demultiplexer_1_out31), .clk(clock_1_out), .Q(reg31_q));  // open: clr
  Multiplexer #(.enable("false"), .select(5), .width(32)) multiplexer_1 (
    .in0({32{1'b0}}), .in1(reg1_q), .in2(reg2_q), .in3(reg3_q), .in4(reg4_q), .in5(reg5_q), .in6(reg6_q),
    .in7(reg7_q), .in8(reg8_q), .in9(reg9_q), .in10(reg10_q), .in11(reg11_q), .in12(reg12_q), .in13(reg13_q),
    .in14(reg14_q), .in15(reg15_q), .in16(reg16_q), .in17(reg17_q), .in18(reg18_q), .in19(reg19_q),
    .in20(reg20_q), .in21(reg21_q), .in22(reg22_q), .in23(reg23_q), .in24(reg24_q), .in25(reg25_q),
    .in26(reg26_q), .in27(reg27_q), .in28(reg28_q), .in29(reg29_q), .in30(reg30_q), .in31(reg31_q),
    .out(rt_data), .sel(rt_select));
  Multiplexer #(.enable("false"), .select(5), .width(32)) multiplexer_2 (
    .in0({32{1'b0}}), .in1(reg1_q), .in2(reg2_q), .in3(reg3_q), .in4(reg4_q), .in5(reg5_q), .in6(reg6_q),
    .in7(reg7_q), .in8(reg8_q), .in9(reg9_q), .in10(reg10_q), .in11(reg11_q), .in12(reg12_q), .in13(reg13_q),
    .in14(reg14_q), .in15(reg15_q), .in16(reg16_q), .in17(reg17_q), .in18(reg18_q), .in19(reg19_q),
    .in20(reg20_q), .in21(reg21_q), .in22(reg22_q), .in23(reg23_q), .in24(reg24_q), .in25(reg25_q),
    .in26(reg26_q), .in27(reg27_q), .in28(reg28_q), .in29(reg29_q), .in30(reg30_q), .in31(reg31_q),
    .out(rs_data), .sel(rs_select));
endmodule

// 5
module ALU (
  input  [31:0] In1,
  input  [31:0] In2,
  input  [2:0] signal1,
  output [31:0] outp
);

  wire and_1_out, clock_1_out, comparator_1_eq, comparator_1_gt, comparator_1_lt, not_1_out;
  wire [31:0] adder_1_out, bit_extender_2_out, bit_extender_3_out, LO_q, multiplier_1_out, shifter_1_out,
       shifter_2_out, subtractor_1_out;

  Multiplier #(.width(32)) multiplier_1 (.a(In1), .b(In2), .out(multiplier_1_out));  // open: cin, cout
  Register #(.width(32)) LO (.D(multiplier_1_out), .en(and_1_out), .clk(clock_1_out), .Q(LO_q));  // open: clr
  Clock clock_1 (.out(clock_1_out));
  Adder #(.width(32)) adder_1 (.a(In1), .b(In2), .out(adder_1_out));  // open: cin, cout
  Subtractor #(.width(32)) subtractor_1 (.a(In1), .b(In2), .out(subtractor_1_out));  // open: bin, bout
  Shifter #(.width(32)) shifter_1 (.in(In1), .\dist (In2[4:0]), .out(shifter_1_out));
  Shifter #(.shift("lr"), .width(32)) shifter_2 (.in(In1), .\dist (In2[4:0]), .out(shifter_2_out));
  Comparator #(.width(32)) comparator_1 (
    .a(In1), .b(In2), .gt(comparator_1_gt), .eq(comparator_1_eq), .lt(comparator_1_lt));
  Bit_Extender #(.in_width(1), .out_width(32)) bit_extender_1 (.in(comparator_1_gt));  // open: out
  assign bit_extender_2_out = {{31{comparator_1_eq}}, comparator_1_eq};  // Bit_Extender bit_extender_2
  assign bit_extender_3_out = {{31{comparator_1_lt}}, comparator_1_lt};  // Bit_Extender bit_extender_3
  Multiplexer #(.enable("false"), .select(3), .width(32)) multiplexer_1 (
    .in0(bit_extender_2_out), .in1(adder_1_out), .in2(subtractor_1_out), .in3(shifter_1_out),
    .in4(shifter_2_out), .in5({32{1'b0}}), .in6(LO_q), .in7(bit_extender_3_out), .out(outp), .sel(signal1));
  not not_1 (not_1_out, signal1[1]);
  and and_1 (and_1_out, signal1[0], not_1_out, signal1[2]);
endmodule

module Control (
  input  [31:0] Instruction,
  output jalSig,
  output j_jalSig,
  output lwswSig,
  output beqSig,
  output weMem,
  output bneSig,
  output [4:0] rs_select,
  output opSignal,
  output [4:0] rt_select,
  output [4:0] rd_select,
  output [31:0] last16bits,
  output [31:0] shamt,
  output we,
  output jrSig,
  output [2:0] controlSig,
  output shamtSig,
  output iSig
);

  wire add_out, and_1_out, and_2_out, and_4_out, and_5_out, and_6_out, and_7_out, and_8_out, and_9_out,
       and_10_out, and_14_out, and_15_out, and_16_out, and_17_out, j_out, lw_out, mflo_out, mult_out,
       multiplexer_1_out, nor_1_out, nor_2_out, nor_3_out, nor_4_out, not_1_out, not_2_out, not_3_out,
       not_4_out, not_5_out, not_6_out, not_7_out, not_8_out, not_9_out, not_10_out, not_11_out, not_12_out,
       not_13_out, not_14_out, not_15_out, not_16_out, not_17_out, not_18_out, not_19_out, not_20_out,
       not_21_out, not_22_out, not_23_out, not_24_out, not_25_out, not_26_out, not_27_out, not_28_out,
       not_29_out, not_30_out, not_31_out, not_32_out, not_33_out, not_34_out, not_35_out, not_36_out,
       not_37_out, not_38_out, not_39_out, not_40_out, not_41_out, not_42_out, not_43_out, not_44_out,
       not_45_out, not_46_out, not_47_out, not_48_out, not_49_out, not_50_out, not_51_out, not_52_out,
       not_53_out, not_54_out, not_55_out, not_56_out, not_57_out, not_58_out, not_59_out, not_60_out,
       not_61_out, not_62_out, not_63_out, not_64_out, or_3_out, or_4_out, or_5_out, or_6_out, or_7_out,
       or_8_out, sleftl_out, slt_out, srightl_out, sub_out, sw_out;
  wire [2:0] and_11_out, multiplexer_7_out, multiplexer_8_out, multiplexer_9_out, multiplexer_10_out,
       multiplexer_11_out, multiplexer_12_out, multiplexer_13_out;

  not not_1 (not_1_out, Instruction[31]);
  not not_2 (not_2_out, Instruction[30]);
  not not_3 (not_3_out, Instruction[29]);
  and beq (beqSig, not_1_out, not_2_out, not_3_out, Instruction[28], not_4_out, not_5_out);
  not not_4 (not_4_out, Instruction[27]);
  not not_5 (not_5_out, Instruction[26]);
  not not_6 (not_6_out, Instruction[31]);
  not not_7 (not_7_out, Instruction[30]);
  not not_8 (not_8_out, Instruction[29]);
  and bne (bneSig, not_6_out, not_7_out, not_8_out, Instruction[28], not_9_out, Instruction[26]);
  not not_9 (not_9_out, Instruction[27]);
  or or_1 (opSignal, multiplexer_1_out, bneSig, beqSig);
  not not_10 (not_10_out, Instruction[5]);
  not not_11 (not_11_out, Instruction[4]);
  and and_1 (and_1_out, not_10_out, not_11_out, Instruction[3], not_12_out, not_13_out, not_14_out);
  not not_12 (not_12_out, Instruction[2]);
  not not_13 (not_13_out, Instruction[1]);
  not not_14 (not_14_out, Instruction[0]);
  not not_15 (not_15_out, Instruction[31]);
  not not_16 (not_16_out, Instruction[26]);
  not not_17 (not_17_out, Instruction[29]);
  and and_2 (and_2_out, not_15_out, not_16_out, not_17_out, not_18_out, not_19_out, not_20_out);
  not not_18 (not_18_out, Instruction[28]);
  not not_19 (not_19_out, Instruction[27]);
  not not_20 (not_20_out, Instruction[30]);
  not not_21 (not_21_out, Instruction[31]);
  not not_22 (not_22_out, Instruction[30]);
  not not_23 (not_23_out, Instruction[29]);
  not not_24 (not_24_out, Instruction[28]);
  not not_25 (not_25_out, Instruction[31]);
  not not_26 (not_26_out, Instruction[30]);
  not not_27 (not_27_out, Instruction[29]);
  not not_28 (not_28_out, Instruction[28]);
  not not_29 (not_29_out, Instruction[26]);
  not not_30 (not_30_out, Instruction[30]);
  not not_31 (not_31_out, Instruction[29]);
  not not_32 (not_32_out, Instruction[28]);
  not not_33 (not_33_out, Instruction[30]);
  not not_34 (not_34_out, Instruction[28]);
  not not_35 (not_35_out, Instruction[31]);
  not not_36 (not_36_out, Instruction[30]);
  not not_37 (not_37_out, Instruction[28]);
  not not_38 (not_38_out, Instruction[27]);
  not not_39 (not_39_out, Instruction[26]);
  and and_3 (jrSig, and_1_out, and_2_out);
  and jal (jalSig, not_21_out, not_22_out, not_23_out, not_24_out, Instruction[27], Instruction[26]);
  and j (j_out, not_25_out, not_26_out, not_27_out, not_28_out, Instruction[27], not_29_out);
  and lw (lw_out, Instruction[31], not_30_out, not_31_out, not_32_out, Instruction[27], Instruction[26]);
  and sw (sw_out, Instruction[31], not_33_out, Instruction[29], not_34_out, Instruction[27], Instruction[26]);
  and and_4 (and_4_out, not_35_out, not_36_out, Instruction[29], not_37_out, not_38_out, not_39_out);
  or or_2 (j_jalSig, jalSig, j_out);
  or or_3 (or_3_out, lw_out, sw_out);
  Multiplexer #(.enable("false")) multiplexer_1 (.in0(1'b1), .in1(1'b0), .out(multiplexer_1_out), .sel(and_4_out));
  and and_5 (and_5_out, multiplexer_1_out, not_54_out);
  Multiplexer #(.enable("false")) multiplexer_2 (.in0(1'b0), .in1(1'b1), .out(lwswSig), .sel(or_3_out));
  and and_6 (and_6_out, Instruction[5], 1'b1);
  nor nor_1 (nor_1_out, Instruction[4], Instruction[3], Instruction[2], Instruction[1], Instruction[0]);
  and and_7 (and_7_out, Instruction[5], Instruction[1]);
  nor nor_2 (nor_2_out, Instruction[4], Instruction[3], Instruction[2], Instruction[0]);
  and and_8 (and_8_out, Instruction[4], Instruction[3]);
  nor nor_3 (nor_3_out, Instruction[1], Instruction[0], Instruction[2], Instruction[5]);
  and and_9 (and_9_out, Instruction[4], Instruction[1]);
  nor nor_4 (nor_4_out, Instruction[2], Instruction[3], Instruction[0], Instruction[5]);
  not not_40 (not_40_out, Instruction[4]);
  not not_41 (not_41_out, Instruction[3]);
  not not_42 (not_42_out, Instruction[2]);
  not not_43 (not_43_out, Instruction[1]);
  not not_44 (not_44_out, Instruction[0]);
  not not_45 (not_45_out, Instruction[5]);
  not not_46 (not_46_out, Instruction[4]);
  not not_47 (not_47_out, Instruction[3]);
  not not_48 (not_48_out, Instruction[2]);
  not not_49 (not_49_out, Instruction[0]);
  not not_50 (not_50_out, Instruction[5]);
  not not_51 (not_51_out, Instruction[4]);
  not not_52 (not_52_out, Instruction[2]);
  not not_53 (not_53_out, Instruction[0]);
  Multiplexer #(.enable("false")) multiplexer_3 (.in0(1'b0), .in1(1'b1), .out(weMem), .sel(sw_out));
  Multiplexer #(.enable("false"), .width(5)) multiplexer_4 (
    .in0(Instruction[25:21]), .in1(Instruction[25:21]), .out(rs_select), .sel(multiplexer_1_out));
  Multiplexer #(.enable("false"), .width(5)) multiplexer_5 (
    .in0(Instruction[20:16]), .in1(Instruction[20:16]), .out(rt_select), .sel(multiplexer_1_out));
  Multiplexer #(.enable("false"), .width(5)) multiplexer_6 (
    .in0(Instruction[20:16]), .in1(Instruction[15:11]), .out(rd_select), .sel(and_10_out));
  assign last16bits = {{16{Instruction[15]}}, Instruction[15:0]};  // Bit_Extender bit_extender_1
  not not_54 (not_54_out, lwswSig);
  assign shamt = {{27{Instruction[10]}}, Instruction[10:6]};  // Bit_Extender bit_extender_2
  not not_55 (not_55_out, multiplexer_1_out);
  and add (add_out, and_6_out, multiplexer_1_out, nor_1_out);
  and sub (sub_out, and_7_out, and_5_out, nor_2_out);
  and mult (mult_out, and_8_out, and_5_out, nor_3_out);
  and mflo (mflo_out, and_9_out, and_5_out, nor_4_out);
  and sleftl (sleftl_out, not_40_out, not_41_out, not_42_out, and_5_out, not_43_out, not_44_out, not_45_out);
  and srightl (srightl_out, not_46_out, and_5_out, Instruction[1], not_47_out, not_48_out, not_49_out, not_50_out);
  and slt (slt_out, Instruction[3], and_5_out, Instruction[1], not_51_out, Instruction[5], not_52_out, not_53_out);
  or or_4 (or_4_out, lwswSig, not_55_out, add_out);
  Multiplexer #(.enable("false"), .width(3)) multiplexer_7 (
    .in0(3'b000), .in1(3'b010), .out(multiplexer_7_out), .sel(sub_out));
  Multiplexer #(.enable("false"), .width(3)) multiplexer_8 (
    .in0(3'b000), .in1(3'b101), .out(multiplexer_8_out), .sel(mult_out));
  Multiplexer #(.enable("false"), .width(3)) multiplexer_9 (
    .in0(3'b000), .in1(3'b110), .out(multiplexer_9_out), .sel(mflo_out));
  Multiplexer #(.enable("false"), .width(3)) multiplexer_10 (
    .in0(3'b000), .in1(3'b011), .out(multiplexer_10_out), .sel(sleftl_out));
  Multiplexer #(.enable("false"), .width(3)) multiplexer_11 (
    .in0(3'b000), .in1(3'b100), .out(multiplexer_11_out), .sel(srightl_out));
  Multiplexer #(.enable("false"), .width(3)) multiplexer_12 (
    .in0(3'b000), .in1(3'b111), .out(multiplexer_12_out), .sel(slt_out));
  Multiplexer #(.enable("false"), .width(3)) multiplexer_13 (
    .in0(3'b000), .in1(3'b001), .out(multiplexer_13_out), .sel(or_4_out));
  and and_10 (and_10_out, not_56_out, multiplexer_1_out);
  not not_56 (not_56_out, lw_out);
  or or_5 (or_5_out, multiplexer_13_out[0], multiplexer_7_out[0], multiplexer_8_out[0], multiplexer_9_out[0], multiplexer_10_out[0], multiplexer_11_out[0], multiplexer_12_out[0]);
  or or_6 (or_6_out, multiplexer_13_out[1], multiplexer_7_out[1], multiplexer_8_out[1], multiplexer_9_out[1], multiplexer_10_out[1], multiplexer_11_out[1], multiplexer_12_out[1]);
  or or_7 (or_7_out, multiplexer_13_out[2], multiplexer_7_out[2], multiplexer_8_out[2], multiplexer_9_out[2], multiplexer_10_out[2], multiplexer_11_out[2], multiplexer_12_out[2]);
  not not_57 (not_57_out, sw_out);
  or or_8 (or_8_out, or_4_out, sub_out, mflo_out, sleftl_out, srightl_out, slt_out);
  and and_11 (and_11_out[0], 1'b1, or_5_out);
  and and_12 (and_11_out[1], multiplexer_1_out, or_6_out);
  and and_13 (and_11_out[2], multiplexer_1_out, or_7_out);
  and and_14 (and_14_out, not_57_out, or_8_out);
  or or_9 (we, jalSig, and_14_out);
  Multiplexer #(.enable("false"), .select(3), .width(3)) multiplexer_14 (
    .in0(3'b000), .in1(3'b001), .in2(3'b010), .in3(3'b011), .in4(3'b100), .in5(3'b101), .in6(3'b110),
    .in7(3'b111), .out(controlSig), .sel(and_11_out));
  not not_58 (not_58_out, and_11_out[2]);
  not not_59 (not_59_out, and_11_out[0]);
  not not_60 (not_60_out, and_11_out[1]);
  not not_61 (not_61_out, and_11_out[0]);
  not not_62 (not_62_out, and_11_out[1]);
  not not_63 (not_63_out, and_11_out[2]);
  and and_15 (and_15_out, and_11_out[0], and_11_out[1], not_58_out);
  and and_16 (and_16_out, not_59_out, not_60_out, and_11_out[2]);
  and and_17 (and_17_out, not_61_out, not_62_out, not_63_out);
  or or_10 (shamtSig, and_15_out, and_16_out);
  not not_64 (not_64_out, multiplexer_1_out);
  or or_11 (iSig, not_64_out, and_17_out);
endmodule

module Processor (
  input  [31:0] DataFromBus,
  output [31:0] DataToBus,
  output [15:0] Address,
  output MemWriteEnable,
  output AddrBusWrite,
  output DataBusWrite
);

  wire and_1_out, and_2_out, clock_1_out, control_1_beqsig, control_1_bnesig, control_1_isig,
       control_1_j_jalsig, control_1_jalsig, control_1_jrsig, control_1_lwswsig, control_1_opsignal,
       control_1_shamtsig, control_1_we, multiplexer_6_out, not_1_out, or_1_out, or_2_out;
  wire [2:0] control_1_controlsig;
  wire [4:0] control_1_rd_select, control_1_rs_select, control_1_rt_select, multiplexer_5_out;
  wire [15:0] adder_1_out, adder_2_out, alu_1_outp, alu_1_outp_2, control_1_last16bits,
       control_1_last16bits_2, multiplexer_1_out, multiplexer_2_out, multiplexer_3_out, register_1_q,
       register_file_1_rs_data, register_file_1_rs_data_2, subtractor_1_out;
  wire [31:0] bit_extender_1_out, control_1_shamt, multiplexer_4_out, multiplexer_7_out, multiplexer_8_out,
       multiplexer_9_out, multiplexer_10_out, multiplexer_11_out, rom_1_data;

  Multiplexer #(.enable("false"), .width(16)) multiplexer_1 (
    .in0(adder_2_out), .in1(control_1_last16bits), .out(multiplexer_1_out), .sel(control_1_j_jalsig));
  Multiplexer #(.enable("false"), .width(16)) multiplexer_2 (
    .in0(multiplexer_1_out), .in1(register_file_1_rs_data), .out(multiplexer_2_out), .sel(control_1_jrsig));
  Multiplexer #(.enable("false"), .width(16)) multiplexer_3 (
    .in0(multiplexer_2_out), .in1(adder_1_out), .out(multiplexer_3_out), .sel(or_1_out));
  Register #(.width(16)) register_1 (
    .D(multiplexer_3_out), .en(1'b1), .clk(clock_1_out), .Q(register_1_q));  // open: clr
  Clock clock_1 (.out(clock_1_out));
  Adder #(.width(16)) adder_1 (.a(control_1_last16bits), .b(subtractor_1_out), .out(adder_1_out));  // open: cin, cout
  Subtractor #(.width(16)) subtractor_1 (.a(adder_2_out), .b(16'h1), .out(subtractor_1_out));  // open: bin, bout
  Adder #(.width(16)) adder_2 (.a(16'h1), .b(register_1_q), .out(adder_2_out));  // open: cin, cout
  ROM #(.addrWidth(16), .dataWidth(32)) rom_1 (.addr(register_1_q), .data(rom_1_data));
  or or_1 (or_1_out, and_1_out, and_2_out);
  and and_1 (and_1_out, alu_1_outp[0], control_1_beqsig);
  and and_2 (and_2_out, not_1_out, control_1_bnesig);
  not not_1 (not_1_out, alu_1_outp[0]);
  assign bit_extender_1_out = {{16{adder_2_out[15]}}, adder_2_out};  // Bit_Extender bit_extender_1
  Control control_1 (
    .Instruction(rom_1_data), .jalSig(control_1_jalsig), .j_jalSig(control_1_j_jalsig),
    .lwswSig(control_1_lwswsig), .beqSig(control_1_beqsig), .weMem(MemWriteEnable),
    .bneSig(control_1_bnesig), .rs_select(control_1_rs_select), .opSignal(control_1_opsignal),
    .rt_select(control_1_rt_select), .rd_select(control_1_rd_select),
    .last16bits({control_1_last16bits_2, control_1_last16bits}), .shamt(control_1_shamt), .we(control_1_we),
    .jrSig(control_1_jrsig), .controlSig(control_1_controlsig), .shamtSig(control_1_shamtsig),
    .iSig(control_1_isig));
  Multiplexer #(.enable("false"), .width(32)) multiplexer_4 (
    .in0(multiplexer_11_out), .in1(bit_extender_1_out), .out(multiplexer_4_out), .sel(control_1_jalsig));
  Multiplexer #(.enable("false"), .width(5)) multiplexer_5 (
    .in0(control_1_rd_select), .in1({5{1'b1}}), .out(multiplexer_5_out), .sel(control_1_jalsig));
  Multiplexer #(.enable("false")) multiplexer_6 (
    .in0(control_1_we), .in1(1'b0), .out(multiplexer_6_out), .sel(control_1_jrsig));
  Register_file register_file_1 (
    .rt_select(control_1_rt_select), .rs_select(control_1_rs_select), .rd_data(multiplexer_4_out),
    .we(multiplexer_6_out), .rd_select(multiplexer_5_out), .rt_data(DataToBus),
    .rs_data({register_file_1_rs_data_2, register_file_1_rs_data}));
  Multiplexer #(.enable("false"), .width(32)) multiplexer_7 (
    .in0({register_file_1_rs_data_2, register_file_1_rs_data}), .in1(DataToBus), .out(multiplexer_7_out),
    .sel(control_1_shamtsig));
  Multiplexer #(.enable("false"), .width(32)) multiplexer_8 (
    .in0(DataToBus), .in1({control_1_last16bits_2, control_1_last16bits}), .out(multiplexer_8_out),
    .sel(or_2_out));
  Multiplexer #(.enable("false"), .width(32)) multiplexer_9 (
    .in0(DataToBus), .in1(control_1_shamt), .out(multiplexer_9_out), .sel(control_1_shamtsig));
  or or_2 (or_2_out, control_1_lwswsig, control_1_isig);
  Multiplexer #(.enable("false"), .width(32)) multiplexer_10 (
    .in0(multiplexer_8_out), .in1(multiplexer_9_out), .out(multiplexer_10_out), .sel(control_1_opsignal));
  Multiplexer #(.enable("false"), .width(32)) multiplexer_11 (
    .in0({alu_1_outp_2, alu_1_outp}), .in1(DataFromBus), .out(multiplexer_11_out), .sel(control_1_lwswsig));
  ALU alu_1 (
    .In1(multiplexer_7_out), .In2(multiplexer_10_out), .signal1(control_1_controlsig),
    .outp({alu_1_outp_2, alu_1_outp}));
  Shifter #(.shift("lr"), .width(16)) shifter_1 (.in(alu_1_outp), .\dist (4'b0010), .out(Address));

  // Notes on the sheet:
  //   contents of rom_1 (hex, n*v repeats v):
  //   201dff00 200800ff afa80013 20040000 20050000 200c0000 20100080 2011ffff 201201f4 20130001 200f0000
  //   20180000 20190000 200e0000 11e00003 ac2822 afa50012 800001e 13000003 8c2020 afa40011 800001e
  //   13200003 ac2820 afa50012 800001e 1320000c 8c2022 afa40011 800001e 224402a 1100002c 225402a 10a0002a
  //   244402a 15000028 245402a 15000026 10900024 8fa90000 1120001b 8fa90001 200d0041 112d0007 200d0041
  //   112d000b 200d0053 112d000f 200d0077 112d0013 800000e 218c0001 200f0001 20180000 20190000 200e0000
  //   800000e 218c0001 20180001 200f0000 20190000 200e0000 8000012 218c0001 20190001 200f0000 20180000
  //   200e0000 8000016 218c0001 200e0001 200f0000 20180000 20190000 800001a 14b0003e afb10013
endmodule

module Memory (
  input  [15:0] AddressFromBus,
  input  MemWriteEnable,
  input  [31:0] DataFromBus,
  output DataBusWrite,
  output [31:0] DataToBus
);

  wire and_1_out, clock_1_out, comparator_1_eq, not_1_out, not_2_out;

  and and_1 (and_1_out, MemWriteEnable, not_2_out);
  Clock clock_1 (.out(clock_1_out));
  Comparator comparator_1 (.a({8{1'b1}}), .b(AddressFromBus[7:0]), .eq(comparator_1_eq));  // open: gt, lt
  RAM #(.addrWidth(16), .dataWidth(32)) ram_1 (
    .addr(AddressFromBus), .we(and_1_out), .oe(1'b1), .clk(clock_1_out), .din(DataFromBus), .dout(DataToBus));
  not not_1 (not_1_out, MemWriteEnable);
  not not_2 (not_2_out, comparator_1_eq);
  and and_2 (DataBusWrite, not_1_out, not_2_out);
endmodule

module KeyboardController (
  input  [31:0] DataFromBus,
  input  BufferKeyboard,
  input  [15:0] AddressFromBus,
  input  [31:0] asciiInput,
  input  MemWriteEnable,
  output [31:0] DataToBus,
  output ReadKeyboard,
  output DataBusWrite
);

  wire and_1_out, and_2_out, bit_extender_1_out, clock_1_out, comparator_1_eq, comparator_2_eq, not_2_out,
       or_1_out, or_2_out;
  wire [31:0] data_q, multiplexer_1_out, status_q;

  and and_1 (and_1_out, BufferKeyboard, ReadKeyboard);
  Comparator #(.width(16)) comparator_1 (.a(16'hff00), .b(AddressFromBus), .eq(comparator_1_eq));  // open: gt, lt
  Multiplexer #(.enable("false"), .width(32)) multiplexer_1 (
    .in0(DataFromBus), .in1(32'h1), .out(multiplexer_1_out), .sel(and_1_out));
  or or_1 (or_1_out, and_1_out, and_2_out);
  and and_2 (and_2_out, comparator_1_eq, MemWriteEnable);
  Register #(.width(32)) status (.D(multiplexer_1_out), .en(or_1_out), .clk(clock_1_out), .Q(status_q));  // open: clr
  Clock clock_1 (.out(clock_1_out));
  Comparator #(.width(16)) comparator_2 (.a(16'hff01), .b(AddressFromBus), .eq(comparator_2_eq));  // open: gt, lt
  Bit_Extender #(.in_width(32), .out_width(1)) bit_extender_1 (.in(status_q), .out(bit_extender_1_out));
  not not_1 (ReadKeyboard, bit_extender_1_out);
  or or_2 (or_2_out, comparator_2_eq, comparator_1_eq);
  and and_3 (DataBusWrite, or_2_out, not_2_out);
  not not_2 (not_2_out, MemWriteEnable);
  Register #(.width(32)) data (.D(asciiInput), .en(and_1_out), .Q(data_q));  // open: clk, clr
  Multiplexer #(.enable("false"), .width(32)) multiplexer_2 (
    .in0(status_q), .in1(data_q), .out(DataToBus), .sel(comparator_2_eq));
endmodule

module VideoController (
  input  [31:0] DataFromBus,
  input  [15:0] AddressFromBus,
  input  MemWriteEnable,
  output [31:0] DataToBus,
  output writeE,
  output [7:0] x,
  output [7:0] y,
  output [23:0] RGBVal,
  output reset,
  output DataBusWrite
);

  wire and_1_out, and_2_out, and_3_out, and_4_out, clock_1_out, comparator_1_eq, comparator_2_eq,
       comparator_3_eq, comparator_4_eq, not_1_out, or_1_out, or_2_out;
  wire [31:0] multiplexer_1_out, register_1_q, register_2_q, register_3_q;

  Multiplexer #(.enable("false"), .width(32)) multiplexer_1 (
    .in0(DataFromBus), .in1({32{1'b0}}), .out(multiplexer_1_out), .sel(writeE));
  Comparator #(.width(16)) comparator_1 (.a(16'hff10), .b(AddressFromBus), .eq(comparator_1_eq));  // open: gt, lt
  Comparator #(.width(16)) comparator_2 (.a(AddressFromBus), .b(16'hff11), .eq(comparator_2_eq));  // open: gt, lt
  Comparator #(.width(16)) comparator_3 (.a(AddressFromBus), .b(16'hff12), .eq(comparator_3_eq));  // open: gt, lt
  Comparator #(.width(16)) comparator_4 (.a(AddressFromBus), .b(16'hff13), .eq(comparator_4_eq));  // open: gt, lt
  and and_1 (and_1_out, comparator_2_eq, MemWriteEnable);
  and and_2 (and_2_out, comparator_3_eq, MemWriteEnable);
  and and_3 (and_3_out, MemWriteEnable, comparator_1_eq);
  and and_4 (and_4_out, comparator_4_eq, MemWriteEnable);
  or or_1 (or_1_out, writeE, and_3_out);
  or or_2 (or_2_out, comparator_4_eq, comparator_3_eq, comparator_2_eq, comparator_1_eq);
  Clock clock_1 (.out(clock_1_out));
  Register #(.width(32)) status (.D(multiplexer_1_out), .en(or_1_out), .clk(clock_1_out), .Q(DataToBus));  // open: clr
  and and_5 (DataBusWrite, or_2_out, not_1_out);
  not not_1 (not_1_out, MemWriteEnable);
  Bit_Extender #(.in_width(32), .out_width(1)) bit_extender_1 (.in(DataToBus), .out(writeE));
  Register #(.width(32)) register_1 (
    .D(multiplexer_1_out), .en(and_1_out), .clk(clock_1_out), .Q(register_1_q));  // open: clr
  Register #(.width(32)) register_2 (
    .D(multiplexer_1_out), .en(and_2_out), .clk(clock_1_out), .Q(register_2_q));  // open: clr
  Register #(.width(32)) register_3 (
    .D(multiplexer_1_out), .en(and_4_out), .clk(clock_1_out), .Q(register_3_q));  // open: clr
  Bit_Extender #(.in_width(32), .out_width(8)) bit_extender_2 (.in(register_1_q), .out(x));
  Bit_Extender #(.in_width(32), .out_width(8)) bit_extender_3 (.in(register_2_q), .out(y));
  Bit_Extender #(.in_width(32), .out_width(24)) bit_extender_4 (.in(register_3_q), .out(RGBVal));
  Comparator #(.width(32)) comparator_5 (.a(register_3_q), .b({32{1'b1}}), .eq(reset));  // open: gt, lt
endmodule

module main (
  input  [15:0] in_1,
  input  in_2,
  input  in_3,
  input  [15:0] in_4,
  input  in_5,
  input  in_6,
  input  [15:0] in_7,
  input  in_8,
  input  in_9,
  output [15:0] out_10,
  output [31:0] out_11,
  output out_12,
  output [15:0] out_13,
  output [31:0] out_14,
  output out_15,
  output [15:0] out_16,
  output [31:0] out_17,
  output out_18,
  output [15:0] AddrOut,
  output [31:0] DataOut,
  output out_21
);

  wire clock_1_out, keyboard_1_avail, keyboardcontroller_1_databuswrite, keyboardcontroller_1_readkeyboard,
       memory_1_databuswrite, processor_1_addrbuswrite, processor_1_databuswrite, processor_1_memwriteenable,
       videocontroller_1_databuswrite, videocontroller_1_reset, videocontroller_1_writee;
  wire [6:0] keyboard_1_data;
  wire [7:0] videocontroller_1_x, videocontroller_1_y;
  wire [15:0] processor_1_address;
  wire [23:0] videocontroller_1_rgbval;
  wire [31:0] bit_extender_1_out, keyboardcontroller_1_datatobus, memory_1_datatobus, processor_1_datatobus,
       videocontroller_1_datatobus;

  assign AddrOut = processor_1_addrbuswrite ? processor_1_address : 16'bz;  // Controlled_Buffer controlled_buffer_1
  Processor processor_1 (
    .DataFromBus(DataOut), .DataToBus(processor_1_datatobus), .Address(processor_1_address),
    .MemWriteEnable(processor_1_memwriteenable), .AddrBusWrite(processor_1_addrbuswrite),
    .DataBusWrite(processor_1_databuswrite));
  assign DataOut = processor_1_databuswrite ? processor_1_datatobus : 32'bz;  // Controlled_Buffer controlled_buffer_2
  assign out_12 = 1'b1 ? processor_1_memwriteenable : 1'bz;  // Controlled_Buffer controlled_buffer_3
  assign AddrOut = 1'b0 ? in_1 : 16'bz;  // Controlled_Buffer controlled_buffer_4
  Memory memory_1 (
    .AddressFromBus(AddrOut), .MemWriteEnable(out_12), .DataFromBus(DataOut),
    .DataBusWrite(memory_1_databuswrite), .DataToBus(memory_1_datatobus));
  assign DataOut = memory_1_databuswrite ? memory_1_datatobus : 32'bz;  // Controlled_Buffer controlled_buffer_5
  Clock clock_1 (.out(clock_1_out));
  assign out_12 = in_3 ? in_2 : 1'bz;  // Controlled_Buffer controlled_buffer_6
  Keyboard keyboard_1 (
    .clk(clock_1_out), .re(keyboardcontroller_1_readkeyboard), .avail(keyboard_1_avail),
    .data(keyboard_1_data));  // open: clr
  assign AddrOut = 1'b0 ? in_4 : 16'bz;  // Controlled_Buffer controlled_buffer_7
  KeyboardController keyboardcontroller_1 (
    .DataFromBus(DataOut), .BufferKeyboard(keyboard_1_avail), .AddressFromBus(AddrOut),
    .asciiInput(bit_extender_1_out), .MemWriteEnable(out_12), .DataToBus(keyboardcontroller_1_datatobus),
    .ReadKeyboard(keyboardcontroller_1_readkeyboard), .DataBusWrite(keyboardcontroller_1_databuswrite));
  assign bit_extender_1_out = {{25{keyboard_1_data[6]}}, keyboard_1_data};  // Bit_Extender bit_extender_1
  assign DataOut = keyboardcontroller_1_databuswrite ? keyboardcontroller_1_datatobus : 32'bz;  // Controlled_Buffer controlled_buffer_8
  assign out_12 = in_6 ? in_5 : 1'bz;  // Controlled_Buffer controlled_buffer_9
  assign AddrOut = 1'b0 ? in_7 : 16'bz;  // Controlled_Buffer controlled_buffer_10
  VideoController videocontroller_1 (
    .DataFromBus(DataOut), .AddressFromBus(AddrOut), .MemWriteEnable(out_12),
    .DataToBus(videocontroller_1_datatobus), .writeE(videocontroller_1_writee), .x(videocontroller_1_x),
    .y(videocontroller_1_y), .RGBVal(videocontroller_1_rgbval), .reset(videocontroller_1_reset),
    .DataBusWrite(videocontroller_1_databuswrite));
  assign DataOut = videocontroller_1_databuswrite ? videocontroller_1_datatobus : 32'bz;  // Controlled_Buffer controlled_buffer_11
  // RGB_Video #(.height(256), .scale(3), .width(256)) rgb_video_1: pin names not known; wires that end beside it: videocontroller_1_reset, clock_1_out, videocontroller_1_writee, videocontroller_1_x, videocontroller_1_y, videocontroller_1_rgbval
  assign out_12 = in_9 ? in_8 : 1'bz;  // Controlled_Buffer controlled_buffer_12

  assign out_10 = AddrOut;
  assign out_11 = DataOut;
  assign out_13 = AddrOut;
  assign out_14 = DataOut;
  assign out_15 = out_12;
  assign out_16 = AddrOut;
  assign out_17 = DataOut;
  assign out_18 = out_12;
  assign out_21 = out_12;
endmodule
